# Fritzing sketch circuit (saved by Fritzing 0.9.4)
circuit board: 8.46667cm x 5.64444cm
breadboards: 1

parts:
  元件1 = node32s
  元件2 = Bluetooth HC-05 Macho
  DHT1 = DHT11 Humitidy and Temperature Sensor
  IR1 = TSOP312.., 314.. [package=THT]
  元件3 = ws2812b [package="smd 2812b"]  # not connected
  LED1 = LED - 5mm [color="Red (633nm)" package="5 mm [THT]"]

nets:
  GND: 元件1.V_BATT, 元件2.GND, DHT1.GND, IR1.GND, LED1.cathode
  N1: 元件1.IO9, 元件2.TXD
  N2: 元件1.IO10, 元件2.RXD
  5V: 元件1.5V, 元件2.VCC, DHT1.VDD, IR1.Vs, LED1.anode
  N3: 元件1.IO4, DHT1.DATA
  N4: 元件1.IO0, IR1.Data

custom parts:
  DHT11 Humitidy and Temperature Sensor: DHT11 Humidity and Temperature Sensor
