# Fritzing sketch KelonAir Conditioner (saved by Fritzing 0.9.8b)
circuit board: 2.61109cm x 2.58816cm

parts:
  DHT1 = DHT11 Humitidy and Temperature Sensor
  U1 = ESP8266 WiFi Module [part_number=ESP8266]
  D1 = LTE-302 [package=lte-302]
  Q1 = TRANSISTOR_NPN [part_number=2N222 package=to-92-ammo]
  R1 = Resistor [tolerance=±5% resistance=1k package="2010 [SMD]"]

nets:
  VDD: DHT1.VDD, U1.VCC, U1.CH_PD, D1.A
  N1: DHT1.DATA, U1.GPIO_2
  GND: DHT1.GND, U1.GND, Q1.E
  N2: U1.RXD, R1.Pin_1
  N3: D1.C, Q1.C
  N4: Q1.B, R1.Pin_0

custom parts:
  DHT11 Humitidy and Temperature Sensor: DHT11 Humidity and Temperature Sensor
  ESP8266 WiFi Module: Generic WiFi Module based on the ESP8266 with onboard PCB antenna and UART communications
